# Fritzing sketch RCController (saved by Fritzing 0.9.5d)
perfboards: 1

parts:
  Bauteil1 = Arduino Nano (Rev3.0) (ICSP)
  J1 = male pin header, 3 pins [form="♂ (male)"]
  J2 = male pin header, 3 pins [form="♂ (male)"]
  J3 = male pin header, 3 pins [form="♂ (male)"]
  J4 = male pin header, 3 pins [form="♂ (male)"]
  Q1 = PNP-Transistor [package="TO92 [THT]"]
  R1 = Resistor [tolerance=±1% resistance=680 package=THT]
  J5 = male pin header, 3 pins [form="♂ (male)"]
  R2 = Resistor [tolerance=±1% resistance=5.6k package=THT]  # not connected
  J7 = male pin header, 2 pins [form="♂ (male)"]
  J8 = male pin header, 4 pins [form="♂ (male)"]
  R3 = Resistor [tolerance=±1% resistance=220 package=THT]
  R5 = Resistor [tolerance=±1% resistance=220 package=THT]
  R4 = Resistor [tolerance=±1% resistance=220 package=THT]
  J9 = male pin header, 3 pins [form="♂ (male)"]
  Q2 = Basic FET P-Channel [package="TO220 [THT]"]
  R6 = Resistor [tolerance=±1% resistance=10k package=THT]
  R7 = Resistor [tolerance=±1% resistance=220 package=THT]
  R8 = Resistor [tolerance=±5% resistance=220 package=THT]
  J10 = male pin header, 2 pins [form="♂ (male)"]
  R9 = Resistor [tolerance=±5% resistance=220 package=THT]
  J11 = male pin header, 1 pin [form="♂ (male)"]

nets:
  N1: Bauteil1.GND, Q2.source, J10.pin1, R9.Pin_0
  N2: Bauteil1.D2, J9.pin2
  N3: Bauteil1.D3, R1.Pin_1
  N4: Bauteil1.D4, J1.pin1
  N5: Bauteil1.D5, J4.pin1
  N6: Bauteil1.D6, J2.pin3
  N7: Bauteil1.D7, J3.pin3
  N8: Bauteil1.D8, R3.Pin_1
  N9: Bauteil1.D9, R4.Pin_1
  N10: Bauteil1.D10, R5.Pin_1
  N11: Bauteil1.D12/MISO, R7.Pin_1
  N12: Bauteil1.VIN, J4.pin2, J5.pin2
  N13: Bauteil1.5V, J10.pin2
  N14: Bauteil1.A7, R8.Pin_1, R9.Pin_1
  N15: Bauteil1.A5, J7.pin2
  N16: Bauteil1.A4, J7.pin1
  N17: Bauteil1.D13/SCK, J9.pin3
  N18: J1.pin3, Q2.drain
  N19: J2.pin1, J3.pin1
  N20: J2.pin2, J3.pin2
  N21: Q1.E, J5.pin1
  N22: Q1.B, R1.Pin_0
  N23: Q1.C, J9.pin1
  N24: J8.pin2, R5.Pin_0
  N25: J8.pin3, R4.Pin_0
  N26: J8.pin4, R3.Pin_0
  N27: R6.Pin_1, R7.Pin_0
  N28: R8.Pin_0, J11.pin1
